// Logisim project MIPSmonociclo.circ as structural Verilog: 15 circuits, main circuit Main
module DataPath (
  input  RegDST_in,
  input  WriteReg_in,
  input  ALUsrc_in,
  input  MemToReg_in,
  input  MemRead_in,
  input  MemWrite_in,
  input  [1:0] ALUop_in,
  input  Branch_in,
  input  Jmp_in,
  input  clk,
  input  reset,
  output [31:0] saida,
  output [3:0] Opcode
);

  wire and_1_out, ULA_zero;
  wire [3:0] msb_pc_1_out_2;
  wire [4:0] cabo_inteiro_1_rd, cabo_inteiro_1_rs, cabo_inteiro_1_rt, multiplexer_2_out, shamt;
  wire [7:0] addressULA8, funct, PCa;
  wire [17:0] cabo_inteiro_1_offset;
  wire [27:0] cabojump_1_offsetj, d;
  wire [31:0] adder_1_out, adder_2_out, addressULA32, br_1_rs, br_1_rt, conc_j_pc_1_saida, multiplexer_1_out,
       multiplexer_3_out, multiplexer_4_out, multiplexer_5_out, Offset, PCt, shifter_1_out;

  Register #(.width(32)) PC (.D(multiplexer_1_out), .en(1'b1), .Q({PCt[31:10], PCa, PCt[1:0]}), .clk(clk), .clr(reset));
  Multiplexer #(.width(32)) multiplexer_1 (
    .in0(multiplexer_4_out), .in1(conc_j_pc_1_saida), .out(multiplexer_1_out), .sel(Jmp_in));
  ROM #(.dataWidth(32)) rom_1 (.addr(PCa), .data({Opcode, d}));
  cabo_shamt cabo_shamt_1 (.dado({Opcode, d}), .shamt_in(shamt));
  cabo_funct cabo_funct_1 (.dado({Opcode, d}), .funct(funct));
  cabo_inteiro cabo_inteiro_1 (
    .DADO({Opcode, d}), .Offset(cabo_inteiro_1_offset), .rs(cabo_inteiro_1_rs), .rt(cabo_inteiro_1_rt),
    .rd(cabo_inteiro_1_rd));
  caboJump cabojump_1 (.dataj({Opcode, d}), .OffsetJ(cabojump_1_offsetj));
  assign Offset = {{14{cabo_inteiro_1_offset[17]}}, cabo_inteiro_1_offset};  // Bit_Extender bit_extender_1
  Multiplexer #(.width(5)) multiplexer_2 (
    .in0(cabo_inteiro_1_rt), .in1(cabo_inteiro_1_rd), .out(multiplexer_2_out), .sel(RegDST_in));
  Shifter #(.width(32)) shifter_1 (.in(Offset), .\dist (5'b00001), .out(shifter_1_out));
  Adder #(.width(32)) adder_1 (.a({PCt[31:10], PCa, PCt[1:0]}), .b(32'h4), .out(adder_1_out));  // open: cin, cout
  MSB_PC msb_pc_1 (.in_1(adder_1_out), .out_2(msb_pc_1_out_2));
  and and_1 (and_1_out, Branch_in, ULA_zero);
  BR br_1 (
    .rsi(cabo_inteiro_1_rs), .rti(cabo_inteiro_1_rt), .dado(multiplexer_5_out), .wr(multiplexer_2_out),
    .we(WriteReg_in), .clk(clk), .reset(reset), .rs(br_1_rs), .rt(br_1_rt));
  conc_j_pc conc_j_pc_1 (.j(cabojump_1_offsetj), .pc_msb(msb_pc_1_out_2), .saida(conc_j_pc_1_saida));
  Multiplexer #(.width(32)) multiplexer_3 (.in0(Offset), .in1(br_1_rt), .out(multiplexer_3_out), .sel(ALUsrc_in));
  Adder #(.width(32)) adder_2 (.a(adder_1_out), .b(shifter_1_out), .out(adder_2_out));  // open: cin, cout
  ALU ULA (
    .A(br_1_rs), .B(multiplexer_3_out), .shamt_in(shamt), .ALUop(ALUop_in), .funct(funct), .zero(ULA_zero),
    .dado({addressULA32[31:10], addressULA8, addressULA32[1:0]}));
  Multiplexer #(.width(32)) multiplexer_4 (
    .in0(adder_1_out), .in1(adder_2_out), .out(multiplexer_4_out), .sel(and_1_out));
  Multiplexer #(.width(32)) multiplexer_5 (
    .in0({addressULA32[31:10], addressULA8, addressULA32[1:0]}), .in1(saida), .out(multiplexer_5_out),
    .sel(MemToReg_in));
  ROM #(.dataWidth(32)) rom_2 (.addr(addressULA8), .data(saida));

  // Other names for the same wires on the sheet: addressULA32[9:2] = addressULA8; ALUop[1:0] = ALUop_in;
  //   ALUsrc = ALUsrc_in; Branch = Branch_in; Jump = Jmp_in; MemRead = MemRead_in; MemToReg = MemToReg_in;
  //   MemWrite = MemWrite_in; d[31:28] = Opcode; PCt[9:2] = PCa; RegDST = RegDST_in; WriteReg = WriteReg_in

  // Notes on the sheet:
  //   contents of rom_1 (hex, n*v repeats v):
  //   10040000 10080004 888000 50008000
  //   contents of rom_2 (hex, n*v repeats v):
  //   2 3
endmodule

module BR (
  input  [4:0] rsi,
  input  [4:0] rti,
  input  [31:0] dado,
  input  [4:0] wr,
  input  we,
  input  clk,
  input  reset,
  output [31:0] rs,
  output [31:0] rt
);

  wire x0we_t, x1we_t, x2we_t, x3we_t, x4we_t, x5we_t, x6we_t, x7we_t, x8we_t, x9we_t, x10we_t, x11we_t,
       x12we_t, x13we_t, x14we_t, x15we_t, x16we_t, x17we_t, x18we_t, x19we_t, x20we_t, x21we_t, x22we_t,
       x23we_t, x24we_t, x25we_t, x26we_t, x27we_t, x28we_t, x29we_t, x30we_t, x31we_t;
  wire [31:0] x0q_t, x1q_t, x2q_t, x3q_t, x4q_t, x5q_t, x6q_t, x7q_t, x8q_t, x9q_t, x10q_t, x11q_t, x12q_t,
       x13q_t, x14q_t, x15q_t, x16q_t, x17q_t, x18q_t, x19q_t, x20q_t, x21q_t, x22q_t, x23q_t, x24q_t,
       x25q_t, x26q_t, x27q_t, x28q_t, x29q_t, x30q_t, x31q_t;

  Demultiplexer #(.select(5)) demultiplexer_1 (
    .out0(x0we_t), .out1(x1we_t), .out2(x2we_t), .out3(x3we_t), .out4(x4we_t), .out5(x5we_t), .out6(x6we_t),
    .out7(x7we_t), .out8(x8we_t), .out9(x9we_t), .out10(x10we_t), .out11(x11we_t), .out12(x12we_t),
    .out13(x13we_t), .out14(x14we_t), .out15(x15we_t), .out16(x16we_t), .out17(x17we_t), .out18(x18we_t),
    .out19(x19we_t), .out20(x20we_t), .out21(x21we_t), .out22(x22we_t), .out23(x23we_t), .out24(x24we_t),
    .out25(x25we_t), .out26(x26we_t), .out27(x27we_t), .out28(x28we_t), .out29(x29we_t), .out30(x30we_t),
    .out31(x31we_t), .in(we), .sel(wr));
  Register #(.width(32)) x0 (.D(dado), .en(x0we_t), .clk(clk), .Q(x0q_t), .clr(reset));
  Register #(.width(32)) x8 (.D(dado), .en(x8we_t), .clk(clk), .Q(x8q_t), .clr(reset));
  Register #(.width(32)) x16 (.D(dado), .en(x16we_t), .clk(clk), .Q(x16q_t), .clr(reset));
  Register #(.width(32)) x24 (.D(dado), .en(x24we_t), .clk(clk), .Q(x24q_t), .clr(reset));
  Register #(.width(32)) x1 (.D(dado), .en(x1we_t), .clk(clk), .Q(x1q_t), .clr(reset));
  Register #(.width(32)) x9 (.D(dado), .en(x9we_t), .clk(clk), .Q(x9q_t), .clr(reset));
  Register #(.width(32)) x17 (.D(dado), .en(x17we_t), .clk(clk), .Q(x17q_t), .clr(reset));
  Register #(.width(32)) x25 (.D(dado), .en(x25we_t), .clk(clk), .Q(x25q_t), .clr(reset));
  Register #(.width(32)) x2 (.D(dado), .en(x2we_t), .clk(clk), .Q(x2q_t), .clr(reset));
  Register #(.width(32)) x10 (.D(dado), .en(x10we_t), .clk(clk), .Q(x10q_t), .clr(reset));
  Register #(.width(32)) x18 (.D(dado), .en(x18we_t), .clk(clk), .Q(x18q_t), .clr(reset));
  Register #(.width(32)) x26 (.D(dado), .en(x26we_t), .clk(clk), .Q(x26q_t), .clr(reset));
  Register #(.width(32)) x3 (.D(dado), .en(x3we_t), .clk(clk), .Q(x3q_t), .clr(reset));
  Register #(.width(32)) x11 (.D(dado), .en(x11we_t), .clk(clk), .Q(x11q_t), .clr(reset));
  Register #(.width(32)) x19 (.D(dado), .en(x19we_t), .clk(clk), .Q(x19q_t), .clr(reset));
  Register #(.width(32)) x27 (.D(dado), .en(x27we_t), .clk(clk), .Q(x27q_t), .clr(reset));
  Register #(.width(32)) x4 (.D(dado), .en(x4we_t), .clk(clk), .Q(x4q_t), .clr(reset));
  Register #(.width(32)) x12 (.D(dado), .en(x12we_t), .clk(clk), .Q(x12q_t), .clr(reset));
  Register #(.width(32)) x20 (.D(dado), .en(x20we_t), .clk(clk), .Q(x20q_t), .clr(reset));
  Register #(.width(32)) x28 (.D(dado), .en(x28we_t), .clk(clk), .Q(x28q_t), .clr(reset));
  Register #(.width(32)) x5 (.D(dado), .en(x5we_t), .clk(clk), .Q(x5q_t), .clr(reset));
  Register #(.width(32)) x13 (.D(dado), .en(x13we_t), .clk(clk), .Q(x13q_t), .clr(reset));
  Register #(.width(32)) x21 (.D(dado), .en(x21we_t), .clk(clk), .Q(x21q_t), .clr(reset));
  Register #(.width(32)) x29 (.D(dado), .en(x29we_t), .clk(clk), .Q(x29q_t), .clr(reset));
  Register #(.width(32)) x6 (.D(dado), .en(x6we_t), .clk(clk), .Q(x6q_t), .clr(reset));
  Register #(.width(32)) x14 (.D(dado), .en(x14we_t), .clk(clk), .Q(x14q_t), .clr(reset));
  Register #(.width(32)) x22 (.D(dado), .en(x22we_t), .clk(clk), .Q(x22q_t), .clr(reset));
  Register #(.width(32)) x30 (.D(dado), .en(x30we_t), .clk(clk), .Q(x30q_t), .clr(reset));
  Register #(.width(32)) x7 (.D(dado), .en(x7we_t), .clk(clk), .Q(x7q_t), .clr(reset));
  Register #(.width(32)) x15 (.D(dado), .en(x15we_t), .clk(clk), .Q(x15q_t), .clr(reset));
  Register #(.width(32)) x23 (.D(dado), .en(x23we_t), .clk(clk), .Q(x23q_t), .clr(reset));
  Register #(.width(32)) x31 (.D(dado), .en(x31we_t), .clk(clk), .Q(x31q_t), .clr(reset));
  Multiplexer #(.select(5), .width(32)) multiplexer_1 (
    .in0(x0q_t), .in1(x1q_t), .in2(x2q_t), .in3(x3q_t), .in4(x4q_t), .in5(x5q_t), .in6(x6q_t), .in7(x7q_t),
    .in8(x8q_t), .in9(x9q_t), .in10(x10q_t), .in11(x11q_t), .in12(x12q_t), .in13(x13q_t), .in14(x14q_t),
    .in15(x15q_t), .in16(x16q_t), .in17(x17q_t), .in18(x18q_t), .in19(x19q_t), .in20(x20q_t), .in21(x21q_t),
    .in22(x22q_t), .in23(x23q_t), .in24(x24q_t), .in25(x25q_t), .in26(x26q_t), .in27(x27q_t), .in28(x28q_t),
    .in29(x29q_t), .in30(x30q_t), .in31(x31q_t), .out(rs), .sel(rsi));
  Multiplexer #(.select(5), .width(32)) multiplexer_2 (
    .in0(x0q_t), .in1(x1q_t), .in2(x2q_t), .in3(x3q_t), .in4(x4q_t), .in5(x5q_t), .in6(x6q_t), .in7(x7q_t),
    .in8(x8q_t), .in9(x9q_t), .in10(x10q_t), .in11(x11q_t), .in12(x12q_t), .in13(x13q_t), .in14(x14q_t),
    .in15(x15q_t), .in16(x16q_t), .in17(x17q_t), .in18(x18q_t), .in19(x19q_t), .in20(x20q_t), .in21(x21q_t),
    .in22(x22q_t), .in23(x23q_t), .in24(x24q_t), .in25(x25q_t), .in26(x26q_t), .in27(x27q_t), .in28(x28q_t),
    .in29(x29q_t), .in30(x30q_t), .in31(x31q_t), .out(rt), .sel(rti));

  // Other names for the same wires on the sheet: data[31:0] = dado; RegDST[4:0] = wr; rs_t[31:0] = rs;
  //   rsi_t[4:0] = rsi; rt_t[31:0] = rt; rti_t[4:0] = rti; WriteReg = we
endmodule

module ALU (
  input  [31:0] A,
  input  [31:0] B,
  input  [4:0] shamt_in,
  input  [1:0] ALUop,
  input  [7:0] funct,
  output zero,
  output [31:0] dado
);

  wire comparator_1_lt;
  wire [3:0] UC_ULA_x;
  wire [31:0] adder_1_out, and_1_out, bit_extender_1_out, divider_1_out, multiplier_1_out, not1_out,
       or_1_out, shifter_1_out, shifter_2_out, subtractor_1_out, xor_1_out;

  Adder #(.width(32)) adder_1 (.a(A), .b(B), .out(adder_1_out));  // open: cin, cout
  Subtractor #(.width(32)) subtractor_1 (.a(A), .b(B), .out(subtractor_1_out));  // open: bin, bout
  Multiplier #(.width(32)) multiplier_1 (.a(A), .b(B), .out(multiplier_1_out));  // open: cin, cout
  Divider #(.width(32)) divider_1 (.a(A), .b(B), .out(divider_1_out));  // open: upper, rem
  Comparator #(.width(32)) comparator_1 (.a(A), .b(B), .lt(comparator_1_lt));  // open: gt, eq
  assign and_1_out = A & B;  // AND_Gate and_1, 32 bits wide
  assign or_1_out = A | B;  // OR_Gate or_1, 32 bits wide
  assign xor_1_out = A ^ B;  // XOR_Gate xor_1, 32 bits wide
  assign not1_out = ~A;  // NOT_Gate not1, 32 bits wide
  Shifter #(.width(32)) shifter_1 (.in(B), .\dist (shamt_in), .out(shifter_1_out));
  Shifter #(.shift("lr"), .width(32)) shifter_2 (.in(B), .\dist (shamt_in), .out(shifter_2_out));
  assign bit_extender_1_out = {{31{comparator_1_lt}}, comparator_1_lt};  // Bit_Extender bit_extender_1
  Multiplexer #(.select(4), .width(32)) multiplexer_1 (
    .in0(adder_1_out), .in1(subtractor_1_out), .in2(multiplier_1_out), .in3(divider_1_out),
    .in4(bit_extender_1_out), .in5(and_1_out), .in6(or_1_out), .in7(xor_1_out), .in8(not1_out),
    .in9(shifter_1_out), .in10(shifter_2_out), .out(dado), .sel(UC_ULA_x));  // open: in11, in12, in13, in14, in15
  UCULA UC_ULA (.ALUop_in(ALUop), .funct_in(funct), .x(UC_ULA_x));
  nor nor_1 (zero, dado[0], dado[1], dado[2], dado[3], dado[4], dado[5], dado[6], dado[7], dado[8], dado[9], dado[10], dado[11], dado[12], dado[13], dado[14], dado[15], dado[16], dado[17], dado[18], dado[19], dado[20], dado[21], dado[22], dado[23], dado[24], dado[25], dado[26], dado[27], dado[28], dado[29], dado[30], dado[31]);
endmodule

module cabo (
  input  b0,
  input  b1,
  input  b2,
  input  b3,
  input  b4,
  output [4:0] s
);


  assign s = {b4, b3, b2, b1, b0};
endmodule

module cabo_offset (
  input  b0,
  input  b1,
  input  b2,
  input  b3,
  input  b4,
  input  b5,
  input  b6,
  input  b7,
  input  b8,
  input  b9,
  input  b10,
  input  b11,
  input  b12,
  input  b13,
  input  b14,
  input  b15,
  input  b16,
  input  b17,
  output [17:0] s
);


  assign s = {b17, b16, b15, b14, b13, b12, b11, b10, b9, b8, b7, b6, b5, b4, b3, b2, b1, b0};
endmodule

module cabo_inteiro (
  input  [31:0] DADO,
  output [17:0] Offset,
  output [4:0] rs,
  output [4:0] rt,
  output [4:0] rd
);

  cabo cabo_1 (.b0(DADO[18]), .b1(DADO[19]), .b2(DADO[20]), .b3(DADO[21]), .b4(DADO[22]), .s(rt));
  cabo cabo_2 (.b0(DADO[23]), .b1(DADO[24]), .b2(DADO[25]), .b3(DADO[26]), .b4(DADO[27]), .s(rs));
  cabo_offset cabo_offset_1 (
    .b0(DADO[0]), .b1(DADO[1]), .b2(DADO[2]), .b3(DADO[3]), .b4(DADO[4]), .b5(DADO[5]), .b6(DADO[6]),
    .b7(DADO[7]), .b8(DADO[8]), .b9(DADO[9]), .b10(DADO[10]), .b11(DADO[11]), .b12(DADO[12]), .b13(DADO[13]),
    .b14(DADO[14]), .b15(DADO[15]), .b16(DADO[16]), .b17(DADO[17]), .s(Offset));
  cabo cabo_3 (.b0(DADO[13]), .b1(DADO[14]), .b2(DADO[15]), .b3(DADO[16]), .b4(DADO[17]), .s(rd));
endmodule

module caboAddress (
  input  [7:0] Address,
  input  [31:0] Data
);
endmodule

module caboJump (
  input  [31:0] dataj,
  output [27:0] OffsetJ
);


  assign OffsetJ = dataj[27:0];
endmodule

module Main (
  input  reset
);

  wire clk_out, controlpath_1_alusrc_in, controlpath_1_branch, controlpath_1_jump, controlpath_1_memread_in,
       controlpath_1_memtoreg_in, controlpath_1_memwrite_in, controlpath_1_regdst_in,
       controlpath_1_writereg_in;
  wire [1:0] controlpath_1_aluop_in;
  wire [3:0] datapath_1_opcode;
  wire [31:0] datapath_1_saida;

  ControlPath controlpath_1 (
    .Opcode(datapath_1_opcode), .RegDST_in(controlpath_1_regdst_in), .WriteReg_in(controlpath_1_writereg_in),
    .ALUsrc_in(controlpath_1_alusrc_in), .MemToReg_in(controlpath_1_memtoreg_in),
    .MemRead_in(controlpath_1_memread_in), .MemWrite_in(controlpath_1_memwrite_in),
    .ALUop_in(controlpath_1_aluop_in), .Branch(controlpath_1_branch), .Jump(controlpath_1_jump));
  Clock clk (.out(clk_out));
  // Probe on datapath_1_saida
  DataPath datapath_1 (
    .RegDST_in(controlpath_1_regdst_in), .WriteReg_in(controlpath_1_writereg_in),
    .ALUsrc_in(controlpath_1_alusrc_in), .MemToReg_in(controlpath_1_memtoreg_in),
    .MemRead_in(controlpath_1_memread_in), .MemWrite_in(controlpath_1_memwrite_in),
    .ALUop_in(controlpath_1_aluop_in), .Branch_in(controlpath_1_branch), .Jmp_in(controlpath_1_jump),
    .clk(clk_out), .reset(reset), .saida(datapath_1_saida), .Opcode(datapath_1_opcode));
endmodule

module ControlPath (
  input  [3:0] Opcode,
  output RegDST_in,
  output WriteReg_in,
  output ALUsrc_in,
  output MemToReg_in,
  output MemRead_in,
  output MemWrite_in,
  output [1:0] ALUop_in,
  output Branch,
  output Jump
);

  ROM #(.addrWidth(4), .dataWidth(10)) rom_1 (
    .addr(Opcode),
    .data({RegDST_in, WriteReg_in, ALUsrc_in, MemToReg_in, MemRead_in, MemWrite_in, ALUop_in, Branch, Jump}));

  // Notes on the sheet:
  //   contents of rom_1 (hex, n*v repeats v):
  //   388 160 10 86 0 1
endmodule

module UCULA (
  input  [1:0] ALUop_in,
  input  [7:0] funct_in,
  output [3:0] x
);

  wire and_4_out;

  and and_1 (x[3], ALUop_in[1], funct_in[3]);
  and and_2 (x[2], ALUop_in[1], funct_in[2]);
  and and_3 (x[1], ALUop_in[1], funct_in[1]);
  and and_4 (and_4_out, ALUop_in[1], funct_in[0]);
  or or_1 (x[0], and_4_out, ALUop_in[0]);
endmodule

module cabo_shamt (
  input  [31:0] dado,
  output [4:0] shamt_in
);


  assign shamt_in = dado[12:8];
endmodule

module MSB_PC (
  input  [31:0] in_1,
  output [3:0] out_2
);


  assign out_2 = in_1[31:28];
endmodule

module conc_j_pc (
  input  [27:0] j,
  input  [3:0] pc_msb,
  output [31:0] saida
);


  assign saida = {pc_msb, j};
endmodule

module cabo_funct (
  input  [31:0] dado,
  output [7:0] funct
);


  assign funct = dado[7:0];
endmodule
